// Logisim project trafficLight.circ as structural Verilog: 1 circuit, main circuit main
module main (
  input  R,
  output [4:0] out_2
);

  wire and_1_out, and_2_out, clock_1_out, comparator_1_eq, comparator_1_lt, comparator_2_eq, comparator_2_gt,
       comparator_2_lt, comparator_3_eq, comparator_3_gt, comparator_3_lt, or_1_out, or_2_out, or_3_out;
  wire [4:0] adder_1_out, multiplexer_1_out;

  Multiplexer #(.width(5), .enable("false")) multiplexer_1 (
    .in0(adder_1_out), .in1({5{1'b0}}), .out(multiplexer_1_out), .sel(R));
  Clock clock_1 (.out(clock_1_out));
  Register #(.width(5)) register_1 (.D(multiplexer_1_out), .Q(out_2), .clk(clock_1_out));  // open: en, clr
  Adder #(.width(5)) adder_1 (.a(out_2), .b(5'b00001), .out(adder_1_out));  // open: cin, cout
  Comparator #(.width(5), .mode("unsigned")) comparator_1 (
    .a(out_2), .b({5{1'b1}}), .eq(comparator_1_eq), .lt(comparator_1_lt));  // open: gt
  Comparator #(.width(5), .mode("unsigned")) comparator_2 (
    .a(out_2), .b(5'b10011), .gt(comparator_2_gt), .eq(comparator_2_eq), .lt(comparator_2_lt));
  Comparator #(.width(5), .mode("unsigned")) comparator_3 (
    .a(out_2), .b(5'b01101), .gt(comparator_3_gt), .eq(comparator_3_eq), .lt(comparator_3_lt));
  or or_1 (or_1_out, comparator_1_eq, comparator_1_lt);
  or or_2 (or_2_out, comparator_2_eq, comparator_2_lt);
  or or_3 (or_3_out, comparator_3_eq, comparator_3_lt);
  and and_1 (and_1_out, or_1_out, comparator_2_gt);
  and and_2 (and_2_out, or_2_out, comparator_3_gt);
  LED led_1 (.in(and_1_out));
  LED led_2 (.in(and_2_out));
  LED led_3 (.in(or_3_out));
endmodule
